// Logisim project CSC3410-MicroArchitecture.circ as structural Verilog: 32 circuits, main circuit main
// MDR
module main (
);

  wire alu_1_n_flag, alu_1_z_flag, clock_1_out, clock_2_out, decoder_1_out_2, decoder_1_out_3,
       decoder_1_out_4, decoder_1_out_5, decoder_1_out_6, decoder_1_out_7, decoder_1_out_8, decoder_1_out_9,
       decoder_1_out_10, high_bit_1_out_5, mir_1_out_2, mir_1_out_8, mir_1_out_9, mir_1_out_10, mir_1_out_11,
       mir_1_out_12, mir_1_out_13, mir_1_out_14, mir_1_out_15, mir_1_out_16;
  wire [1:0] mir_1_out_5, mir_1_out_6;
  wire [2:0] mir_1_out_3;
  wire [3:0] b_1_out_2, control_store_1_out_3;
  wire [5:0] mir_1_out_7;
  wire [7:0] mbr_1_to_junction_box, ram_1_mbr;
  wire [8:0] mir_1_out_4, mpc_1_out_4, o_1_out_4;
  wire [31:0] alu_1_out_5, control_store_1_out_2, h_1_a_bus, mar_1_output_to_ram, mbr_1_out_7,
       mdr_1_output_to_ram, pc_1_ram_output, ram_1_mdr_2, shifter_1_out_3;

  Clock clock_1 (.out(clock_1_out));
  RAM ram_1 (
    .MAR(mar_1_output_to_ram), .PC(pc_1_ram_output), .MDR_2(ram_1_mdr_2), .clock(clock_1_out),
    .MDR(mdr_1_output_to_ram), .MBR(ram_1_mbr), .WRF(mir_1_out_3));
  Clock #(.highDuration(2), .lowDuration(2)) clock_2 (.out(clock_2_out));
  MBR mbr_1 (
    .Input(ram_1_mbr), .Clock(clock_2_out), .Signed(decoder_1_out_5), .out_7(mbr_1_out_7),
    .out_8(mbr_1_out_7), .Unsigned(decoder_1_out_4), .To_Junction_Box(mbr_1_to_junction_box),
    .in_2(mir_1_out_3));
  SP sp_1 (
    .in_1(shifter_1_out_3), .Clock(clock_2_out), .Enabled(mir_1_out_13), .out_5(mbr_1_out_7),
    .Enable_Output(decoder_1_out_6));
  LV lv_1 (
    .in_1(shifter_1_out_3), .Clock(clock_2_out), .Enabled(mir_1_out_12), .out_5(mbr_1_out_7),
    .Enable_Output(decoder_1_out_7));
  CPP cpp_1 (
    .in_1(shifter_1_out_3), .Clock(clock_2_out), .Enabled(mir_1_out_11), .out_5(mbr_1_out_7),
    .Enable_Output(decoder_1_out_8));
  TOS tos_1 (
    .in_1(shifter_1_out_3), .Clock(clock_2_out), .Enabled(mir_1_out_10), .out_5(mbr_1_out_7),
    .Enable_Output(decoder_1_out_9));
  OPC opc_1 (
    .in_1(shifter_1_out_3), .Clock(clock_2_out), .Enabled(mir_1_out_9), .out_5(mbr_1_out_7),
    .Enable_Output(decoder_1_out_10));
  H h_1 (.C_Bus(shifter_1_out_3), .Clock(clock_2_out), .Enable_C_Bus(mir_1_out_8), .A_Bus(h_1_a_bus));
  ALU alu_1 (
    .Z_Flag(alu_1_z_flag), .in_1(h_1_a_bus), .in_2(mbr_1_out_7), .out_5(alu_1_out_5), .in_3(mir_1_out_7),
    .N_Flag(alu_1_n_flag));  // open: Carry_Out
  MAR mar_1 (
    .Input_from_C_Bus(shifter_1_out_3), .Clock(clock_2_out), .Enable_C_Bus(mir_1_out_16),
    .Output_to_RAM(mar_1_output_to_ram));
  MDR mdr_1 (
    .C_Bus_Input(shifter_1_out_3), .Clock(clock_2_out), .C_Bus_Enabled(mir_1_out_15),
    .B_Bus_Output(mbr_1_out_7), .Enable_B_Bus(decoder_1_out_2), .Input_from_RAM(ram_1_mdr_2),
    .Output_to_RAM(mdr_1_output_to_ram), .WRF(mir_1_out_3));
  PC pc_1 (
    .C_Bus_Input(shifter_1_out_3), .Clock(clock_2_out), .B_Bus_Output(mbr_1_out_7),
    .Enable_B_Bus(decoder_1_out_3), .Enable_C_Bus(mir_1_out_14), .RAM_Output(pc_1_ram_output));
  Shifter shifter_1 (.in_1(alu_1_out_5), .out_3(shifter_1_out_3), .Controls(mir_1_out_6));
  Decoder decoder_1 (
    .in_1(b_1_out_2), .out_2(decoder_1_out_2), .out_3(decoder_1_out_3), .out_4(decoder_1_out_4),
    .out_5(decoder_1_out_5), .out_6(decoder_1_out_6), .out_7(decoder_1_out_7), .out_8(decoder_1_out_8),
    .out_9(decoder_1_out_9), .out_10(decoder_1_out_10));
  High_Bit high_bit_1 (
    .N(alu_1_n_flag), .out_5(high_bit_1_out_5), .in_2(clock_2_out), .JAMN_JAMZ(mir_1_out_5), .Z(alu_1_z_flag));
  MPC mpc_1 (.out_4(mpc_1_out_4), .in_2(high_bit_1_out_5), .in_1(o_1_out_4), .in_3(clock_2_out));
  O o_1 (.ADDR(mir_1_out_4), .out_4(o_1_out_4), .MBR(mbr_1_to_junction_box), .JMPC(mir_1_out_2));
  MIR mir_1 (
    .in_1(control_store_1_out_2), .out_4(mir_1_out_4), .out_5(mir_1_out_5), .out_6(mir_1_out_6),
    .out_7(mir_1_out_7), .out_8(mir_1_out_8), .out_9(mir_1_out_9), .out_10(mir_1_out_10),
    .out_11(mir_1_out_11), .out_3(mir_1_out_3), .out_12(mir_1_out_12), .out_13(mir_1_out_13),
    .out_14(mir_1_out_14), .out_15(mir_1_out_15), .out_16(mir_1_out_16), .out_2(mir_1_out_2));
  Control_Store control_store_1 (.out_2(control_store_1_out_2), .out_3(control_store_1_out_3), .in_1(mpc_1_out_4));
  B b_1 (.in_1(control_store_1_out_3), .out_2(b_1_out_2));

  // Notes on the sheet:
  //   10/20/15
  //   Nick Zayatz
  //   Michele Burns
  //   Michael Newton
  //   Charlie Adams
  //   Main File for CSC3410-MicroArchitecture Project
  //   N
  //   Z
  //   JAMN/JAMZ
endmodule

module Addr (
  input  [8:0] in_1,
  output [8:0] out_2
);


  assign out_2 = in_1;

  // Notes on the sheet:
  //   in_1: pull=down
endmodule

module ALU (
  input  [31:0] in_1,
  input  [31:0] in_2,
  input  [5:0] in_3,
  output Z_Flag,
  output [31:0] out_5,
  output N_Flag,
  output Carry_Out
);

  wire n8bitalu_1_carry_out, n8bitalu_2_carry_out, n8bitalu_3_carry_out;

  _8BitALU u_8bitalu_1 (
    .out_9(out_5[7:0]), .F1(in_3[4]), .F0(in_3[5]), .ENB(in_3[2]), .B(in_2[7:0]), .ENA(in_3[3]),
    .A(in_1[7:0]), .INVA(in_3[1]), .in_8(in_3[0]), .Carry_Out(n8bitalu_1_carry_out));
  _8BitALU u_8bitalu_2 (
    .out_9(out_5[15:8]), .F1(in_3[4]), .F0(in_3[5]), .ENB(in_3[2]), .B(in_2[15:8]), .ENA(in_3[3]),
    .A(in_1[15:8]), .INVA(in_3[1]), .in_8(n8bitalu_1_carry_out), .Carry_Out(n8bitalu_2_carry_out));
  _8BitALU u_8bitalu_3 (
    .out_9(out_5[23:16]), .F1(in_3[4]), .F0(in_3[5]), .ENB(in_3[2]), .B(in_2[23:16]), .ENA(in_3[3]),
    .A(in_1[23:16]), .INVA(in_3[1]), .in_8(n8bitalu_2_carry_out), .Carry_Out(n8bitalu_3_carry_out));
  _8BitALU u_8bitalu_4 (
    .out_9({N_Flag, out_5[30:24]}), .F1(in_3[4]), .F0(in_3[5]), .ENB(in_3[2]), .B(in_2[31:24]),
    .ENA(in_3[3]), .A(in_1[31:24]), .INVA(in_3[1]), .in_8(n8bitalu_3_carry_out), .Carry_Out(Carry_Out));
  nor nor_1 (Z_Flag, out_5[0], out_5[1], out_5[2], out_5[3], out_5[4], out_5[5], out_5[6], out_5[7], out_5[8], out_5[9], out_5[10], out_5[11], out_5[12], out_5[13], out_5[14], out_5[15], out_5[16], out_5[17], out_5[18], out_5[19], out_5[20], out_5[21], out_5[22], out_5[23], out_5[24], out_5[25], out_5[26], out_5[27], out_5[28], out_5[29], out_5[30], N_Flag);

  assign out_5[31] = N_Flag;

  // Notes on the sheet:
  //   Carry In
  //   INVA
  //   A
  //   ENA
  //   B
  //   ENB
  //   F0
  //   F1
  //   Output
endmodule

// ALU
module ALU___Control (
  input  [7:0] in_1,
  output [1:0] out_2,
  output [5:0] out_3
);


  assign out_2 = in_1[7:6];
  assign out_3 = in_1[5:0];
endmodule

module B (
  input  [3:0] in_1,
  output [3:0] out_2
);


  assign out_2 = in_1;
endmodule

module C (
  input  [8:0] in_1,
  output out_2,
  output out_3,
  output out_4,
  output out_5,
  output out_6,
  output out_7,
  output out_8,
  output out_9,
  output out_10
);


  assign out_2 = in_1[8];
  assign out_3 = in_1[7];
  assign out_4 = in_1[6];
  assign out_5 = in_1[5];
  assign out_6 = in_1[4];
  assign out_7 = in_1[3];
  assign out_8 = in_1[2];
  assign out_9 = in_1[1];
  assign out_10 = in_1[0];
endmodule

module Control_Store (
  input  [8:0] in_1,
  output [31:0] out_2,
  output [3:0] out_3
);

  ROM #(.addrWidth(9), .dataWidth(32)) rom_1 (.addr(in_1), .data(out_2));  // open: sel
  ROM #(.addrWidth(9), .dataWidth(4)) rom_2 (.addr(in_1), .data(out_3));  // open: sel

  // Notes on the sheet:
  //   in_1: pull=down
endmodule

module CPP (
  input  [31:0] in_1,
  input  Enabled,
  input  Clock,
  input  Enable_Output,
  output [31:0] out_5
);

  wire [31:0] bit_extender_1_out, register_1_q;

  Register #(.width(32)) register_1 (.D(in_1), .en(Enabled), .Q(register_1_q), .clk(Clock));  // open: clr
  assign bit_extender_1_out = {{31{Enable_Output}}, Enable_Output};  // Bit_Extender bit_extender_1
  assign out_5 = register_1_q & bit_extender_1_out;  // AND_Gate and_1, 32 bits wide

  // Notes on the sheet:
  //   Output
endmodule

module Decoder (
  input  [3:0] in_1,
  output out_2,
  output out_3,
  output out_4,
  output out_5,
  output out_6,
  output out_7,
  output out_8,
  output out_9,
  output out_10
);

  Decoder_part #(.select(4)) decoder_1 (
    .out0(out_2), .out1(out_3), .out2(out_4), .out3(out_5), .out4(out_6), .out5(out_7), .out6(out_8),
    .out7(out_9), .out8(out_10), .sel(in_1));  // open: out9, out10, out11, out12, out13, out14, out15, en
endmodule

module H (
  input  [31:0] C_Bus,
  input  Enable_C_Bus,
  input  Clock,
  output [31:0] A_Bus
);

  Register #(.width(32)) register_1 (.D(C_Bus), .en(Enable_C_Bus), .Q(A_Bus), .clk(Clock));  // open: clr
endmodule

module High_Bit (
  input  N,
  input  in_2,
  input  [1:0] JAMN_JAMZ,
  input  Z,
  output out_5
);

  wire and_1_out, and_2_out, d_ff_1_q, d_ff_2_q;

  D_Flip_Flop d_ff_1 (.clk(in_2), .D(N), .Q(d_ff_1_q));  // open: Qn, preset, en, reset
  D_Flip_Flop d_ff_2 (.clk(in_2), .D(Z), .Q(d_ff_2_q));  // open: Qn, preset, en, reset
  and and_1 (and_1_out, d_ff_1_q, JAMN_JAMZ[1]);
  and and_2 (and_2_out, JAMN_JAMZ[0], d_ff_2_q);
  or or_1 (out_5, and_1_out, and_2_out);
endmodule

module J (
  input  [2:0] in_1,
  output out_2,
  output [1:0] out_3
);


  assign out_2 = in_1[2];
  assign out_3 = in_1[1:0];

  // Notes on the sheet:
  //   in_1: pull=down
endmodule

module LV (
  input  [31:0] in_1,
  input  Enabled,
  input  Clock,
  input  Enable_Output,
  output [31:0] out_5
);

  wire [31:0] bit_extender_1_out, register_1_q;

  Register #(.width(32)) register_1 (.D(in_1), .en(Enabled), .Q(register_1_q), .clk(Clock));  // open: clr
  assign bit_extender_1_out = {{31{Enable_Output}}, Enable_Output};  // Bit_Extender bit_extender_1
  assign out_5 = register_1_q & bit_extender_1_out;  // AND_Gate and_1, 32 bits wide

  // Notes on the sheet:
  //   Output
endmodule

module M (
  input  [2:0] in_1,
  output [2:0] out_2
);


  assign out_2 = in_1;
endmodule

module MAR (
  input  [31:0] Input_from_C_Bus,
  input  Clock,
  input  Enable_C_Bus,
  output [31:0] Output_to_RAM
);

  Register #(.width(32)) register_1 (
    .D(Input_from_C_Bus), .en(Enable_C_Bus), .Q(Output_to_RAM), .clk(Clock));  // open: clr
endmodule

module MBR (
  input  [7:0] Input,
  input  [2:0] in_2,
  input  Clock,
  input  Signed,
  input  Unsigned,
  output [7:0] To_Junction_Box,
  output [31:0] out_7,
  output [31:0] out_8
);

  wire [31:0] bit_extender_1_out, bit_extender_2_out, bit_extender_3_out, bit_extender_4_out;

  Register register_1 (.D(Input), .en(in_2[0]), .Q(To_Junction_Box), .clk(Clock));  // open: clr
  assign bit_extender_1_out = {{31{Signed}}, Signed};  // Bit_Extender bit_extender_1
  assign bit_extender_2_out = {{24{To_Junction_Box[7]}}, To_Junction_Box};  // Bit_Extender bit_extender_2
  assign bit_extender_3_out = {{24{1'b0}}, To_Junction_Box};  // Bit_Extender bit_extender_3
  assign bit_extender_4_out = {{31{Unsigned}}, Unsigned};  // Bit_Extender bit_extender_4
  assign out_7 = bit_extender_1_out & bit_extender_2_out;  // AND_Gate and_1, 32 bits wide
  assign out_8 = bit_extender_3_out & bit_extender_4_out;  // AND_Gate and_2, 32 bits wide

  // Notes on the sheet:
  //   Signed Output
  //   Unsigned Output
endmodule

module MDR (
  input  [2:0] WRF,
  input  [31:0] Input_from_RAM,
  input  Clock,
  input  C_Bus_Enabled,
  input  Enable_B_Bus,
  input  [31:0] C_Bus_Input,
  output [31:0] Output_to_RAM,
  output [31:0] B_Bus_Output
);

  wire or_1_out, read, write;
  wire [31:0] and_1_out, and_2_out, bit_extender_1_out, bit_extender_2_out, bit_extender_3_out,
       bit_extender_4_out, or_2_out, register_1_q;

  WRF_Splitter wrf_splitter_1 (.WRF(WRF), .Read(read), .Write(write));  // open: Fetch
  assign bit_extender_1_out = {{31{read}}, read};  // Bit_Extender bit_extender_1
  or or_1 (or_1_out, read, C_Bus_Enabled);
  assign bit_extender_2_out = {{31{C_Bus_Enabled}}, C_Bus_Enabled};  // Bit_Extender bit_extender_2
  assign and_1_out = Input_from_RAM & bit_extender_1_out;  // AND_Gate and_1, 32 bits wide
  assign or_2_out = and_1_out | and_2_out;  // OR_Gate or_2, 32 bits wide
  assign and_2_out = bit_extender_2_out & C_Bus_Input;  // AND_Gate and_2, 32 bits wide
  assign bit_extender_3_out = {{31{write}}, write};  // Bit_Extender bit_extender_3
  Register #(.width(32)) register_1 (.D(or_2_out), .en(or_1_out), .Q(register_1_q), .clk(Clock));  // open: clr
  assign bit_extender_4_out = {{31{Enable_B_Bus}}, Enable_B_Bus};  // Bit_Extender bit_extender_4
  assign Output_to_RAM = bit_extender_3_out & register_1_q;  // AND_Gate and_3, 32 bits wide
  assign B_Bus_Output = register_1_q & bit_extender_4_out;  // AND_Gate and_4, 32 bits wide
endmodule

module MIR (
  input  [31:0] in_1,
  output out_2,
  output [2:0] out_3,
  output [8:0] out_4,
  output [1:0] out_5,
  output [1:0] out_6,
  output [5:0] out_7,
  output out_8,
  output out_9,
  output out_10,
  output out_11,
  output out_12,
  output out_13,
  output out_14,
  output out_15,
  output out_16
);

  Addr addr_1 (.in_1(in_1[31:23]), .out_2(out_4));
  J j_1 (.in_1(in_1[22:20]), .out_3(out_5), .out_2(out_2));
  ALU___Control alu_control_1 (.in_1(in_1[19:12]), .out_2(out_6), .out_3(out_7));
  C c_1 (
    .in_1(in_1[11:3]), .out_2(out_8), .out_3(out_9), .out_4(out_10), .out_5(out_11), .out_6(out_12),
    .out_7(out_13), .out_8(out_14), .out_9(out_15), .out_10(out_16));
  M m_1 (.in_1(in_1[2:0]), .out_2(out_3));
endmodule

module MPC (
  input  [8:0] in_1,
  input  in_2,
  input  in_3,
  output [8:0] out_4
);

  wire [8:0] bit_extender_1_out, or_1_out;

  assign bit_extender_1_out = {{8{1'b0}}, in_2};  // Bit_Extender bit_extender_1
  assign or_1_out = in_1 | bit_extender_1_out;  // OR_Gate or_1, 9 bits wide
  Register #(.width(9)) register_1 (.D(or_1_out), .Q(out_4), .clk(in_3));  // open: en, clr
endmodule

module O (
  input  [8:0] ADDR,
  input  [7:0] MBR,
  input  JMPC,
  output [8:0] out_4
);

  wire [8:0] and_1_out, and_2_out, bit_extender_1_out, bit_extender_2_out, not_1_out, or_1_out;

  assign bit_extender_1_out = {{1{MBR[7]}}, MBR};  // Bit_Extender bit_extender_1
  assign bit_extender_2_out = {{8{JMPC}}, JMPC};  // Bit_Extender bit_extender_2
  assign or_1_out = ADDR | bit_extender_1_out;  // OR_Gate or_1, 9 bits wide
  assign not_1_out = ~bit_extender_2_out;  // NOT_Gate not_1, 9 bits wide
  assign and_1_out = ADDR & not_1_out;  // AND_Gate and_1, 9 bits wide
  assign and_2_out = or_1_out & bit_extender_2_out;  // AND_Gate and_2, 9 bits wide
  assign out_4 = and_1_out | and_2_out;  // OR_Gate or_2, 9 bits wide
endmodule

module OPC (
  input  [31:0] in_1,
  input  Enabled,
  input  Clock,
  input  Enable_Output,
  output [31:0] out_5
);

  wire [31:0] bit_extender_1_out, register_1_q;

  Register #(.width(32)) register_1 (.D(in_1), .en(Enabled), .Q(register_1_q), .clk(Clock));  // open: clr
  assign bit_extender_1_out = {{31{Enable_Output}}, Enable_Output};  // Bit_Extender bit_extender_1
  assign out_5 = register_1_q & bit_extender_1_out;  // AND_Gate and_1, 32 bits wide

  // Notes on the sheet:
  //   Output
endmodule

module PC (
  input  [31:0] C_Bus_Input,
  input  Enable_C_Bus,
  input  Clock,
  input  Enable_B_Bus,
  output [31:0] RAM_Output,
  output [31:0] B_Bus_Output
);

  wire [31:0] bit_extender_1_out;

  Register #(.width(32)) register_1 (.D(C_Bus_Input), .en(Enable_C_Bus), .Q(RAM_Output), .clk(Clock));  // open: clr
  assign bit_extender_1_out = {{31{Enable_B_Bus}}, Enable_B_Bus};  // Bit_Extender bit_extender_1
  assign B_Bus_Output = RAM_Output & bit_extender_1_out;  // AND_Gate and_1, 32 bits wide
endmodule

module RAM (
  input  [2:0] WRF,
  input  [31:0] MAR,
  input  clock,
  input  [31:0] MDR,
  input  [31:0] PC,
  output [31:0] MDR_2,
  output [7:0] MBR
);

  wire and_3_out, Counter, fetch, not_2_out, not_3_out, or_1_out, read, write;
  wire [1:0] ctr;
  wire [7:0] multiplexer_1_out;
  wire [23:0] and_1_out, and_2_out, bit_extender_1_out, bit_extender_3_out, bit_extender_4_out,
       bit_extender_5_out, not_1_out, or_2_out;
  wire [23:2] bit_extender_2_out;
  wire [31:0] buffer_1_out, ram_1_data;

  Counter #(.width(1), .max('h1), .trigger("falling")) counter_1 (
    .Q(Counter), .clk(clock));  // open: load, D, count, carry, clr
  WRF_Splitter wrf_splitter_1 (.WRF(WRF), .Fetch(fetch), .Read(read), .Write(write));
  assign bit_extender_1_out = {{23{Counter}}, Counter};  // Bit_Extender bit_extender_1
  Bit_Extender #(.in_width(32), .out_width(24), .\type ("sign")) bit_extender_2 (
    .in(PC), .out({bit_extender_2_out, ctr}));
  Bit_Extender #(.in_width(32), .out_width(24), .\type ("sign")) bit_extender_3 (.in(MAR), .out(bit_extender_3_out));
  or or_1 (or_1_out, read, write);
  assign bit_extender_4_out = {{23{or_1_out}}, or_1_out};  // Bit_Extender bit_extender_4
  assign bit_extender_5_out = {{23{fetch}}, fetch};  // Bit_Extender bit_extender_5
  assign and_1_out = bit_extender_3_out & bit_extender_4_out & not_1_out;  // AND_Gate and_1, 24 bits wide
  assign not_1_out = ~bit_extender_1_out;  // NOT_Gate not_1, 24 bits wide
  assign and_2_out = bit_extender_1_out & bit_extender_5_out & {2'b00, bit_extender_2_out};  // AND_Gate and_2, 24 bits wide
  assign or_2_out = and_1_out | and_2_out;  // OR_Gate or_2, 24 bits wide
  not not_2 (not_2_out, Counter);
  RAM_part #(.addrWidth(24), .dataWidth(32), .bus("separate")) ram_1 (
    .addr(or_2_out), .din(MDR), .data(ram_1_data), .str(write), .clk(clock), .ld(not_3_out));  // open: sel, clr
  not not_3 (not_3_out, and_3_out);
  and and_3 (and_3_out, not_2_out, write);
  assign buffer_1_out = ram_1_data;  // Buffer buffer_1, 32 bits wide
  Multiplexer #(.select(2), .width(8)) multiplexer_1 (
    .in0(buffer_1_out[31:24]), .in1(buffer_1_out[23:16]), .in2(buffer_1_out[15:8]), .in3(buffer_1_out[7:0]),
    .out(multiplexer_1_out), .sel(ctr));  // open: en
  Register #(.width(32), .trigger("falling")) register_1 (
    .D(buffer_1_out), .en(read), .Q(MDR_2), .clk(Counter));  // open: clr
  Register #(.trigger("falling")) register_2 (.D(multiplexer_1_out), .en(fetch), .Q(MBR), .clk(Counter));  // open: clr
endmodule

module Shifter (
  input  [31:0] in_1,
  input  [1:0] Controls,
  output [31:0] out_3
);

  wire [31:0] demultiplexer_1_out0, demultiplexer_1_out1, demultiplexer_1_out2, demultiplexer_1_out3,
       shifter_1_out, shifter_2_out, undriven;

  Demultiplexer #(.select(2), .width(32)) demultiplexer_1 (
    .out0(demultiplexer_1_out0), .out1(demultiplexer_1_out1), .out2(demultiplexer_1_out2),
    .out3(demultiplexer_1_out3), .in(in_1), .sel(Controls));  // open: en
  Shifter_part #(.width(32), .shift("ar")) shifter_1 (
    .in(demultiplexer_1_out1), .\dist (5'b00001), .out(shifter_1_out));
  Shifter_part #(.width(32)) shifter_2 (.in(demultiplexer_1_out2), .\dist (5'b01000), .out(shifter_2_out));
  Multiplexer #(.select(2), .width(32)) multiplexer_1 (
    .in0(demultiplexer_1_out0), .in1(shifter_1_out), .in2(shifter_2_out), .in3(undriven), .out(out_3),
    .sel(Controls));  // open: en

  // Notes on the sheet:
  //   Input
  //   Shifter
  //   Output
endmodule

module SP (
  input  [31:0] in_1,
  input  Enabled,
  input  Clock,
  input  Enable_Output,
  output [31:0] out_5
);

  wire [31:0] bit_extender_1_out, register_1_q;

  Register #(.width(32)) register_1 (.D(in_1), .en(Enabled), .Q(register_1_q), .clk(Clock));  // open: clr
  assign bit_extender_1_out = {{31{Enable_Output}}, Enable_Output};  // Bit_Extender bit_extender_1
  assign out_5 = register_1_q & bit_extender_1_out;  // AND_Gate and_1, 32 bits wide

  // Notes on the sheet:
  //   Output
endmodule

module TOS (
  input  [31:0] in_1,
  input  Enabled,
  input  Clock,
  input  Enable_Output,
  output [31:0] out_5
);

  wire [31:0] bit_extender_1_out, register_1_q;

  Register #(.width(32)) register_1 (.D(in_1), .en(Enabled), .Q(register_1_q), .clk(Clock));  // open: clr
  assign bit_extender_1_out = {{31{Enable_Output}}, Enable_Output};  // Bit_Extender bit_extender_1
  assign out_5 = register_1_q & bit_extender_1_out;  // AND_Gate and_1, 32 bits wide

  // Notes on the sheet:
  //   Output
endmodule

module Wired_Machine (
);

  MAR mar_1 ();  // open: Input_from_C_Bus, Clock, Enable_C_Bus, Output_to_RAM
  MBR mbr_1 ();  // open: Input, Clock, Signed, out_7, out_8, Unsigned, To_Junction_Box, in_2
  SP sp_1 ();  // open: in_1, Clock, Enabled, out_5, Enable_Output
  LV lv_1 ();  // open: in_1, Clock, Enabled, out_5, Enable_Output
  CPP cpp_1 ();  // open: in_1, Clock, Enabled, out_5, Enable_Output
  TOS tos_1 ();  // open: in_1, Clock, Enabled, out_5, Enable_Output
  OPC opc_1 ();  // open: in_1, Clock, Enabled, out_5, Enable_Output
  H h_1 ();  // open: C_Bus, Clock, Enable_C_Bus, A_Bus
  ALU alu_1 ();  // open: Z_Flag, in_1, in_2, out_5, in_3, N_Flag, Carry_Out
  MDR mdr_1 ();  // open: C_Bus_Input, Clock, C_Bus_Enabled, B_Bus_Output, Enable_B_Bus, Input_from_RAM, Output_to_RAM, WRF
  PC pc_1 ();  // open: C_Bus_Input, Clock, B_Bus_Output, Enable_B_Bus, Enable_C_Bus, RAM_Output
  Shifter shifter_1 ();  // open: in_1, out_3, Controls
  Decoder decoder_1 ();  // open: in_1, out_2, out_3, out_4, out_5, out_6, out_7, out_8, out_9, out_10
  High_Bit high_bit_1 ();  // open: N, out_5, in_2, JAMN_JAMZ, Z
  MPC mpc_1 ();  // open: out_4, in_2, in_1, in_3
  O o_1 ();  // open: ADDR, out_4, MBR, JMPC
  Addr addr_1 ();  // open: in_1, out_2
  J j_1 ();  // open: in_1, out_3, out_2
  ALU___Control alu_control_1 ();  // open: in_1, out_2, out_3
  Control_Store control_store_1 ();  // open: out_2, out_3, in_1
  C c_1 ();  // open: in_1, out_2, out_3, out_4, out_5, out_6, out_7, out_8, out_9, out_10
  M m_1 ();  // open: in_1, out_2
  B b_1 ();  // open: in_1, out_2
endmodule

module _1BitAdder (
  input  Carry_In,
  input  A,
  input  B,
  input  Function,
  output Result,
  output Carry_Out
);

  wire and_1_out, and_2_out, xor_1_out, xor_2_out;

  and and_1 (and_1_out, Function, B, A);
  or or_1 (Carry_Out, and_1_out, and_2_out);
  xor xor_1 (xor_1_out, A, B);
  and and_2 (and_2_out, Function, xor_1_out, Carry_In);
  xor xor_2 (xor_2_out, Carry_In, xor_1_out);
  and and_3 (Result, xor_2_out, Function);
endmodule

module _1BitALU (
  input  Carry_In,
  input  A,
  input  ENA,
  input  B,
  input  ENB,
  input  in_6,
  input  F1,
  input  F0,
  output Output,
  output out_10
);

  wire and_1_out, and_2_out, and_3_out, and_4_out, and_5_out, and_6_out, decoder_1_out0, decoder_1_out1,
       decoder_1_out2, decoder_1_out3, n1bitadder_1_result, not_1_out, or_1_out, xor_1_out;

  and and_1 (and_1_out, ENA, B);
  and and_2 (and_2_out, ENB, in_6);
  xor xor_1 (xor_1_out, A, and_1_out);
  not not_1 (not_1_out, and_2_out);
  Decoder_part #(.select(2)) decoder_1 (
    .out0(decoder_1_out0), .out1(decoder_1_out1), .out2(decoder_1_out2), .out3(decoder_1_out3), .sel({F0, F1}));  // open: en
  and and_3 (and_3_out, xor_1_out, and_2_out);
  or or_1 (or_1_out, xor_1_out, and_2_out);
  and and_4 (and_4_out, and_3_out, decoder_1_out0);
  and and_5 (and_5_out, or_1_out, decoder_1_out1);
  and and_6 (and_6_out, not_1_out, decoder_1_out2);
  _1BitAdder u_1bitadder_1 (
    .A(and_2_out), .B(xor_1_out), .Function(decoder_1_out3), .Result(n1bitadder_1_result),
    .Carry_In(Carry_In), .Carry_Out(out_10));
  or or_2 (Output, and_4_out, and_5_out, and_6_out, n1bitadder_1_result);

  // Notes on the sheet:
  //   INVA
endmodule

module _8BitALU (
  input  F1,
  input  F0,
  input  ENB,
  input  [7:0] B,
  input  ENA,
  input  [7:0] A,
  input  INVA,
  input  in_8,
  output [7:0] out_9,
  output Carry_Out
);

  wire n1bitalu_2_out_10, n1bitalu_3_out_10, n1bitalu_4_out_10, n1bitalu_5_out_10, n1bitalu_6_out_10,
       n1bitalu_7_out_10, n1bitalu_8_out_10;

  _1BitALU u_1bitalu_1 (
    .Carry_In(n1bitalu_2_out_10), .A(INVA), .ENA(A[7]), .B(ENA), .ENB(B[7]), .in_6(ENB), .F1(F1), .F0(F0),
    .Output(out_9[7]), .out_10(Carry_Out));
  _1BitALU u_1bitalu_2 (
    .Carry_In(n1bitalu_3_out_10), .A(INVA), .ENA(A[6]), .B(ENA), .ENB(B[6]), .in_6(ENB), .F1(F1), .F0(F0),
    .Output(out_9[6]), .out_10(n1bitalu_2_out_10));
  _1BitALU u_1bitalu_3 (
    .Carry_In(n1bitalu_4_out_10), .A(INVA), .ENA(A[5]), .B(ENA), .ENB(B[5]), .in_6(ENB), .F1(F1), .F0(F0),
    .Output(out_9[5]), .out_10(n1bitalu_3_out_10));
  _1BitALU u_1bitalu_4 (
    .Carry_In(n1bitalu_5_out_10), .A(INVA), .ENA(A[4]), .B(ENA), .ENB(B[4]), .in_6(ENB), .F1(F1), .F0(F0),
    .Output(out_9[4]), .out_10(n1bitalu_4_out_10));
  _1BitALU u_1bitalu_5 (
    .Carry_In(n1bitalu_6_out_10), .A(INVA), .ENA(A[3]), .B(ENA), .ENB(B[3]), .in_6(ENB), .F1(F1), .F0(F0),
    .Output(out_9[3]), .out_10(n1bitalu_5_out_10));
  _1BitALU u_1bitalu_6 (
    .Carry_In(n1bitalu_7_out_10), .A(INVA), .ENA(A[2]), .B(ENA), .ENB(B[2]), .in_6(ENB), .F1(F1), .F0(F0),
    .Output(out_9[2]), .out_10(n1bitalu_6_out_10));
  _1BitALU u_1bitalu_7 (
    .Carry_In(n1bitalu_8_out_10), .A(INVA), .ENA(A[1]), .B(ENA), .ENB(B[1]), .in_6(ENB), .F1(F1), .F0(F0),
    .Output(out_9[1]), .out_10(n1bitalu_7_out_10));
  _1BitALU u_1bitalu_8 (
    .Carry_In(in_8), .A(INVA), .ENA(A[0]), .B(ENA), .ENB(B[0]), .in_6(ENB), .F1(F1), .F0(F0),
    .Output(out_9[0]), .out_10(n1bitalu_8_out_10));

  // Notes on the sheet:
  //   Out
  //   Carry In
endmodule

module _32BitALU (
  input  [31:0] in_1,
  input  [31:0] in_2,
  input  [5:0] in_3,
  output Z_Flag,
  output [31:0] out_5,
  output N_Flag,
  output Carry_Out
);

  wire n8bitalu_1_p9, n8bitalu_2_p10, n8bitalu_3_p10;

  // _8BitALU 8bitalu_1: pin names not known; wires that end beside it: in_3[1], in_1[7:0], in_3[3], in_2[7:0], in_3[2], in_3[5], in_3[4], in_3[0], n8bitalu_1_p9, out_5[7:0], out_5[15:8]
  // _8BitALU 8bitalu_2: pin names not known; wires that end beside it: in_3[1], in_1[15:8], in_3[3], in_2[15:8], in_3[2], in_3[5], in_3[4], n8bitalu_1_p9, n8bitalu_1_p9, n8bitalu_2_p10, out_5[15:8]
  // _8BitALU 8bitalu_3: pin names not known; wires that end beside it: in_3[1], in_1[23:16], in_3[3], in_2[23:16], in_3[2], in_3[5], in_3[4], n8bitalu_2_p10, n8bitalu_2_p10, n8bitalu_3_p10, out_5[23:16]
  // _8BitALU 8bitalu_4: pin names not known; wires that end beside it: in_3[1], in_1[31:24], in_3[3], in_2[31:24], in_3[2], in_3[5], in_3[4], n8bitalu_3_p10, n8bitalu_3_p10, Carry_Out, {N_Flag, out_5[30:24]}
  nor nor_1 (Z_Flag, out_5[0], out_5[1], out_5[2], out_5[3], out_5[4], out_5[5], out_5[6], out_5[7], out_5[8], out_5[9], out_5[10], out_5[11], out_5[12], out_5[13], out_5[14], out_5[15], out_5[16], out_5[17], out_5[18], out_5[19], out_5[20], out_5[21], out_5[22], out_5[23], out_5[24], out_5[25], out_5[26], out_5[27], out_5[28], out_5[29], out_5[30], N_Flag);

  assign out_5[31] = N_Flag;

  // Notes on the sheet:
  //   Carry In
  //   INVA
  //   A
  //   ENA
  //   B
  //   ENB
  //   F0
  //   F1
  //   Output
endmodule

module WRF_Splitter (
  input  [2:0] WRF,
  output Fetch,
  output Read,
  output Write
);


  assign Fetch = WRF[0];
  assign Read = WRF[1];
  assign Write = WRF[2];
endmodule
